# Fritzing sketch circuit (saved by Fritzing 0.9.3b)
breadboards: 1

parts:
  Raspberry_Pi1 = Raspberry Pi B rev2
  POT_ROUND_STRIP = Neopixel Strip -- White (60/m)
  STEM_1 = Neopixel Strip -- White (60/m)
  STEM_2 = Neopixel Strip -- White (60/m)
  STEM_3 = Neopixel Strip -- White (60/m)

nets:
  +5V: Raspberry_Pi1.5V, POT_ROUND_STRIP.+5V, STEM_1.+5V, STEM_2.+5V, STEM_3.+5V
  GND: Raspberry_Pi1.GND, POT_ROUND_STRIP.GND, STEM_1.GND, STEM_2.GND, STEM_3.GND
  N1: Raspberry_Pi1.GPIO_14, POT_ROUND_STRIP.DI
  N2: POT_ROUND_STRIP.DO, STEM_1.DI
  N3: STEM_1.DO, STEM_2.DI
  N4: STEM_2.DO, STEM_3.DI

notes:
  There is SPLixel Basic - RGB LED Controller in between..
  1. UART TX -> DI (SPLixel Basic - RGB LED Controller) -> DI (POT ROUND STRIP)
  2. 5V -> 5V (SPLixel Basic - RGB LED Controller)
  3. GND -> GND (SPLixel Basic - RGB LED Controller)

custom parts:
  Neopixel Strip -- White (60/m): Neopixel Strip, White, 60 pixels per meter.
