# Fritzing sketch circuit (saved by Fritzing 0.9.3b)
breadboards: 1

parts:
  23LCV1 = 23LCV1024 [part_number=23LCV1024 package="DIP (Dual Inline) [THT]"]
  D1 = Rectifier Diode [part_number=1N4001 package="300 mil [THT]"]
  Part1 = Arduino Uno (Rev3)
  D2 = Rectifier Diode [part_number=1N4001 package="300 mil [THT]"]
  D3 = Rectifier Diode [part_number=1N4001 package="300 mil [THT]"]
  D4 = Rectifier Diode [part_number=1N4001 package="300 mil [THT]"]
  VCC1 = Battery block 9V

nets:
  N1: 23LCV1.SO/SIO1, Part1.D5_PWM
  N2: 23LCV1.NC, D1.anode, Part1.GND, D2.anode, VCC1.-
  N3: 23LCV1.VSS, Part1.D3_PWM
  N4: 23LCV1.SI/SIO0, D2.cathode, D4.anode
  N5: 23LCV1.SCK, D3.cathode, D4.cathode, VCC1.+
  N6: 23LCV1.VBAT, D1.cathode
